# Fritzing sketch CO2_K-30_UART (saved by Fritzing 0.9.3b)

parts:
  K1 = CO2 sensor [package=PCB]
  MCU = Arduino Mega 2560 (Rev3)
  +6-9VDC1 = Power plug
  K2 = CO2 sensor [package=PCB]
  +6-9VDC2 = Power plug
  K3 = CO2 sensor [package=PCB]
  +6-9VDC3 = Power plug
  K4 = CO2 sensor [package=PCB]
  +6-9VDC4 = Power plug
  K5 = CO2 sensor [package=PCB]
  +6-9VDC5 = Power plug
  K6 = CO2 sensor [package=PCB]
  +6-9VDC6 = Power plug
  K7 = CO2 sensor [package=PCB]
  +6-9VDC7 = Power plug
  K8 = CO2 sensor [package=PCB]
  +6-9VDC8 = Power plug
  K9 = CO2 sensor [package=PCB]
  +6-9VDC9 = Power plug
  K10 = CO2 sensor [package=PCB]
  +6-9VDC10 = Power plug
  K11 = CO2 sensor [package=PCB]
  +6-9VDC11 = Power plug
  K12 = CO2 sensor [package=PCB]
  +6-9VDC12 = Power plug
  K13 = CO2 sensor [package=PCB]
  +6-9VDC13 = Power plug
  K14 = CO2 sensor [package=PCB]
  +6-9VDC14 = Power plug
  K15 = CO2 sensor [package=PCB]
  +6-9VDC15 = Power plug
  K16 = CO2 sensor [package=PCB]
  +6-9VDC16 = Power plug
  K17 = CO2 sensor [package=PCB]
  +6-9VDC17 = Power plug

nets:
  GND: K1.G0, MCU.GND, +6-9VDC1.GND, K2.G0, +6-9VDC2.GND, K3.G0, +6-9VDC3.GND, K4.G0, +6-9VDC4.GND, K5.G0, +6-9VDC5.GND, K6.G0, +6-9VDC6.GND, K7.G0, +6-9VDC7.GND, K8.G0, +6-9VDC8.GND, K9.G0, +6-9VDC9.GND, K10.G0, +6-9VDC10.GND, K11.G0, +6-9VDC11.GND, K12.G0, +6-9VDC12.GND, K13.G0, +6-9VDC13.GND, K14.G0, +6-9VDC14.GND, K15.G0, +6-9VDC15.GND, K16.G0, +6-9VDC16.GND, K17.G0, +6-9VDC17.GND
  N1: K1.G+, +6-9VDC1.VCC
  N2: K1.RxD_UART, MCU.D18/TX1
  N3: K1.TxD_UART, MCU.D19/RX1
  N4: MCU.A8, K12.TxD_UART
  N5: MCU.A9, K13.TxD_UART
  N6: MCU.A10, K14.TxD_UART
  N7: MCU.A11, K15.TxD_UART
  N8: MCU.A12, K16.TxD_UART
  N9: MCU.A13, K17.TxD_UART
  N10: MCU.D17_PWM/RX2, K2.TxD_UART
  N11: MCU.D16_PWM/TX2, K2.RxD_UART
  N12: MCU.D15/RX3, K3.TxD_UART
  N13: MCU.D14/TX3, K3.RxD_UART
  N14: MCU.D13_PWM, K7.TxD_UART
  N15: MCU.D12_PWM, K6.TxD_UART
  N16: MCU.D11_PWM, K5.TxD_UART
  N17: MCU.D10_PWM, K4.TxD_UART
  N18: MCU.D2_PWM, K4.RxD_UART
  N19: MCU.D3_PWM, K5.RxD_UART
  N20: MCU.D4_PWM, K6.RxD_UART
  N21: MCU.D5_PWM, K7.RxD_UART
  N22: MCU.D6_PWM, K8.RxD_UART
  N23: MCU.D38, K9.RxD_UART
  N24: MCU.D39, K10.RxD_UART
  N25: MCU.D40, K11.RxD_UART
  N26: MCU.D41, K12.RxD_UART
  N27: MCU.D42, K13.RxD_UART
  N28: MCU.D43, K14.RxD_UART
  N29: MCU.D44, K15.RxD_UART
  N30: MCU.D45, K16.RxD_UART
  N31: MCU.D46, K17.RxD_UART
  N32: MCU.D50, K8.TxD_UART
  N33: MCU.D51, K9.TxD_UART
  N34: MCU.D52, K10.TxD_UART
  N35: MCU.D53, K11.TxD_UART
  N36: K2.G+, +6-9VDC2.VCC
  N37: K3.G+, +6-9VDC3.VCC
  N38: K4.G+, +6-9VDC4.VCC
  N39: K5.G+, +6-9VDC5.VCC
  N40: K6.G+, +6-9VDC6.VCC
  N41: K7.G+, +6-9VDC7.VCC
  N42: K8.G+, +6-9VDC8.VCC
  N43: K9.G+, +6-9VDC9.VCC
  N44: K10.G+, +6-9VDC10.VCC
  N45: K11.G+, +6-9VDC11.VCC
  N46: K12.G+, +6-9VDC12.VCC
  N47: K13.G+, +6-9VDC13.VCC
  N48: K14.G+, +6-9VDC14.VCC
  N49: K15.G+, +6-9VDC15.VCC
  N50: K16.G+, +6-9VDC16.VCC
  N51: K17.G+, +6-9VDC17.VCC

notes:
  PlantConnect, K30 CO2 sensor, 0.1

custom parts:
  CO2 sensor: A CO2 sensor from CO2Meter - K30. Datasheet http://co2meters.com/Documentation/Datasheets/DS30-01%20-%20K30.pdf Could not make fine PCB and principal. You should make yours if needed.
