# Fritzing sketch LightRelays_16 (saved by Fritzing 0.9.3b)
breadboards: 1

parts:
  C3 = Ceramic Capacitor [capacitance=100nF voltage=16V package="100 mil [THT, multilayer]"]
  C4 = Ceramic Capacitor [capacitance=1µF voltage=50V package="100 mil [THT, multilayer]"]
  MCU1 = Arduino Mega 2560 (Rev3)
  8_Channel_Relay1 = 8 Channel Power Relay
  VCC2 = DC Power [voltage=5V]
  VCC1 = DC Power [voltage=24V]
  Light_Panel_8 = female pin header, 2 pins [form="♀ (female)"]
  Light_Panel_7 = female pin header, 2 pins [form="♀ (female)"]
  Light_Panel_6 = female pin header, 2 pins [form="♀ (female)"]
  Light_Panel_5 = female pin header, 2 pins [form="♀ (female)"]
  Light_Panel_4 = female pin header, 2 pins [form="♀ (female)"]
  Light_Panel_3 = female pin header, 2 pins [form="♀ (female)"]
  Light_Panel_2 = female pin header, 2 pins [form="♀ (female)"]
  Light_Panel_1 = female pin header, 2 pins [form="♀ (female)"]
  8_Channel_Relay2 = 8 Channel Power Relay
  Light_Panel_16 = female pin header, 2 pins [form="♀ (female)"]
  Light_Panel_15 = female pin header, 2 pins [form="♀ (female)"]
  Light_Panel_14 = female pin header, 2 pins [form="♀ (female)"]
  Light_Panel_13 = female pin header, 2 pins [form="♀ (female)"]
  Light_Panel_12 = female pin header, 2 pins [form="♀ (female)"]
  Light_Panel_11 = female pin header, 2 pins [form="♀ (female)"]
  Light_Panel_10 = female pin header, 2 pins [form="♀ (female)"]
  Light_Panel_9 = female pin header, 2 pins [form="♀ (female)"]
  C5 = Ceramic Capacitor [capacitance=100nF voltage=16V package="100 mil [THT, multilayer]"]
  C6 = Ceramic Capacitor [capacitance=1µF voltage=50V package="100 mil [THT, multilayer]"]
  VCC4 = DC Power [voltage=5V]
  VCC3 = DC Power [voltage=24V]

nets:
  GND: C3.0, C4.0, 8_Channel_Relay1.GND, VCC2.V-, VCC1.V-, Light_Panel_8.pin2, Light_Panel_7.pin2, Light_Panel_6.pin2, Light_Panel_5.pin2, Light_Panel_4.pin2, Light_Panel_3.pin2, Light_Panel_2.pin2, Light_Panel_1.pin2, 8_Channel_Relay2.GND, C5.0, C6.0, VCC4.V-, VCC3.V-
  N1: C3.1, 8_Channel_Relay1.JD-VCC, VCC2.V+
  N2: C4.1, 8_Channel_Relay1.COM, VCC1.V+
  VCC: MCU1.5V, 8_Channel_Relay1.VCC, 8_Channel_Relay2.VCC
  N3: MCU1.D22, 8_Channel_Relay1.IN1
  N4: MCU1.D23, 8_Channel_Relay1.IN2
  N5: MCU1.D24, 8_Channel_Relay1.IN3
  N6: MCU1.D25, 8_Channel_Relay1.IN4
  N7: MCU1.D26, 8_Channel_Relay1.IN5
  N8: MCU1.D27, 8_Channel_Relay1.IN6
  N9: MCU1.D28, 8_Channel_Relay1.IN7
  N10: MCU1.D29, 8_Channel_Relay1.IN8
  N11: MCU1.D30, 8_Channel_Relay2.IN1
  N12: MCU1.D31, 8_Channel_Relay2.IN2
  N13: MCU1.D32, 8_Channel_Relay2.IN3
  N14: MCU1.D33, 8_Channel_Relay2.IN4
  N15: MCU1.D34, 8_Channel_Relay2.IN5
  N16: MCU1.D35, 8_Channel_Relay2.IN6
  N17: MCU1.D36, 8_Channel_Relay2.IN7
  N18: MCU1.D37, 8_Channel_Relay2.IN8
  N19: 8_Channel_Relay1.NO#23, Light_Panel_1.pin1
  N20: 8_Channel_Relay1.NO#26, Light_Panel_2.pin1
  N21: 8_Channel_Relay1.NO#29, Light_Panel_3.pin1
  N22: 8_Channel_Relay1.NO#32, Light_Panel_4.pin1
  N23: 8_Channel_Relay1.NO#35, Light_Panel_5.pin1
  N24: 8_Channel_Relay1.NO#38, Light_Panel_6.pin1
  N25: 8_Channel_Relay1.NO#41, Light_Panel_7.pin1
  N26: 8_Channel_Relay1.NO#44, Light_Panel_8.pin1
  N27: 8_Channel_Relay2.JD-VCC, C5.1, VCC4.V+
  N28: 8_Channel_Relay2.COM, C6.1, VCC3.V+
  N29: 8_Channel_Relay2.NO#23, Light_Panel_9.pin1
  N30: 8_Channel_Relay2.NO#26, Light_Panel_10.pin1
  N31: 8_Channel_Relay2.NO#29, Light_Panel_11.pin1
  N32: 8_Channel_Relay2.NO#32, Light_Panel_12.pin1
  N33: 8_Channel_Relay2.NO#35, Light_Panel_13.pin1
  N34: 8_Channel_Relay2.NO#38, Light_Panel_14.pin1
  N35: 8_Channel_Relay2.NO#41, Light_Panel_15.pin1
  N36: 8_Channel_Relay2.NO#44, Light_Panel_16.pin1
  N37: Light_Panel_16.pin2, Light_Panel_15.pin2, Light_Panel_14.pin2, Light_Panel_13.pin2, Light_Panel_12.pin2, Light_Panel_11.pin2, Light_Panel_10.pin2, Light_Panel_9.pin2

notes:
  2 8-channel relay boards (or 1 16-channel) for driving the Light panels. Note that the Arduino is NOT conncted to the ground of this circuit. That is because the relay board has an optooscillator (basically an LED and phototransistor) that is used to electrically isolate the relays from the rest of your circuit. This is for safety. The Arduino will be tied to a separate ground
  PlantConnect, 8-channel relay boards, 0.1

custom parts:
  8 Channel Power Relay: An 8 channel power relay. The module operates at 5V.
