# Fritzing sketch MFC_simple_opamp (saved by Fritzing 0.9.3b)
breadboards: 1

parts:
  U1_(LM358) = LM 358 Dual Op-Amp [package="DIP8 [THT]"]
  D1 = Zener Diode [part_number="1N4732A - 5.1V" breakdown_voltage=5.1V package="Melf DO-213 AB [SMD]"]
  MFC = female pin header, 2 pins [form="♀ (female)"]
  R1 = Resistor [tolerance=±5% resistance=47 package=THT]
  R2 = Resistor [tolerance=±5% resistance=1k package=THT]
  R3 = Resistor [tolerance=±5% resistance=10k package=THT]
  to_Arduino = male pin header, 1 pin [form="♂ (male)"]

nets:
  N1: U1_(LM358).connector0, R3.Pin_1, to_Arduino.pin1
  N2: U1_(LM358).connector2, R2.Pin_1, R3.Pin_0
  GND: U1_(LM358).connector3, D1.anode, MFC.pin2, R1.Pin_0
  5V: U1_(LM358).connector7
  N3: D1.cathode, MFC.pin1, R1.Pin_1, R2.Pin_0

notes:
  MFC voltage amplifier
  This schematic includes an op-amp (operational amplifier) to boost the signal coming from the MFC (which is often very low, e.g. in the millivolt range)
  R1 is simply a load for the MFC (may not be necessary and can vary from about 10ohms to 1K)
  The 5.1v Zener diode (D1) ensures that we do not send more than 5v to the Arduino
  R2 & R3 affect the amplication factor of the op-amp. In this case the 1K and 10K resitors gives us an amplication factor of 10
  PlantConnect, MFC/Bioelectricity amplifier
